# Fritzing sketch bytebee85-production-planb (saved by Fritzing 0.9.9b)
circuit board: 5.00213cm x 4cm
breadboards: 1

parts:
  U2 = attiny85 [package=dip]
  R9 = Resistor [tolerance=±5% power=0.25 resistance=10k package=THT]
  LED2 = LED - 5mm [color="Red (633nm)" current=0.030 package="5 mm [THT]"]
  S2 = Pushbutton [package="[THT]"]
  R10 = Rotary Potentiometer (Large) [maximum_resistance=100kΩ package=THT]
  VCC2 = Battery
  TRS3 = Audio Jack (TRS) 3.5mm [package="4Ucon 08780 [THT]"]
  TRS4 = Audio Jack (TRS) 3.5mm [package="4Ucon 08780 [THT]"]
  R16 = Resistor [tolerance=±5% power=0.25 resistance=10k package=THT]
  R17 = Resistor [tolerance=±5% power=0.25 resistance=10k package=THT]
  R18 = Resistor [tolerance=±5% power=0.25 resistance=1k package=THT]
  C2 = Ceramic Capacitor [capacitance=100nF voltage=35V package="200 mil [THT, multilayer]"]

nets:
  N1: U2.Pin_2, R9.Pin_0, R16.Pin_1, R17.Pin_1, C2.1
  N2: U2.Pin_3, R10.wiper
  GND: U2.Pin_4, S2.Pin_3, S2.Pin_4, R10.leg2, VCC2.-, TRS3.Sleeve, TRS4.Sleeve, R17.Pin_0, R18.Pin_0
  N3: U2.Pin_6, LED2.anode, TRS3.Tip
  3V: U2.Pin_8, R10.leg1, VCC2.+, R16.Pin_0
  N4: R9.Pin_1, S2.Pin_1, S2.Pin_2
  N5: LED2.cathode, R18.Pin_1
  N6: TRS4.Ring, C2.0

notes:
  PROGRAMMER IN (RING)
  Button Left ++
  Pot2
  Bootloader indicator
  AUDIO OUT (TIP)
